# Fritzing sketch Led And Buttons And pca9865 wiring diagram (saved by Fritzing 1.0.5)
breadboards: 1

parts:
  LED1 = RGB LED - (4 legs) [color="Red (633nm)" current=0.030A package="5 mm [THT]"]
  LED2 = RGB LED - (4 legs) [color="Red (633nm)" current=0.030A package="5 mm [THT]"]
  R1 = Resistor [tolerance=±5% resistance=240 package="2010 [SMD]"]  # not connected
  Mod1 = Raspberry Pi 4B
  R2 = Resistor [tolerance=±5% resistance=240 package="2010 [SMD]"]
  R3 = Resistor [tolerance=±5% resistance=240 package="2010 [SMD]"]
  R4 = Resistor [tolerance=±5% resistance=240 package="2010 [SMD]"]
  R5 = Resistor [tolerance=±5% resistance=240 package="2010 [SMD]"]
  R6 = Resistor [tolerance=±5% resistance=240 package="2010 [SMD]"]
  Language = Pushbutton [package="[THT]"]
  modebtn = Pushbutton [package="[THT]"]
  R7 = Resistor [tolerance=±5% resistance=240 package="2010 [SMD]"]
  R8 = Resistor [tolerance=±5% resistance=240 package="2010 [SMD]"]
  J6 = Basic Servo
  J7 = Basic Servo
  J8 = Basic Servo
  J9 = Basic Servo
  J10 = Basic Servo
  Part2 = Adafruit PCA9685 PWM/Servo Breakout [part_number=815]
  V2 = Pulse Power [initial_voltage=0V pulsed_voltage=5V period=100ms pulse_width=50ms duty_cycle=25% number_of_pulses=0 delay_time=0s internal_resistance=0.1Ω]  # not connected

nets:
  GND: LED1.common_anode, LED2.common_anode, Mod1.GND, Language.Pin_1, Language.Pin_2, modebtn.Pin_1, modebtn.Pin_2, J6.gnd, J7.gnd, J8.gnd, J9.gnd, J10.gnd, Part2.GND
  N1: LED1.green_cathode, R2.Pin_1
  N2: LED1.blue_cathode, R3.Pin_1
  N3: LED2.red_cathode, R4.Pin_1
  N4: LED2.green_cathode, R5.Pin_1
  N5: LED2.blue_cathode, R6.Pin_1
  3V3: Mod1.3V3, Part2.VCC
  N6: Mod1.GPIO2, Part2.SDA
  N7: Mod1.GPIO3, Part2.SCL
  N8: Mod1.GPIO17, R7.Pin_1
  N9: Mod1.GPIO27, R8.Pin_1
  N10: Mod1.GPIO6, R2.Pin_0
  N11: Mod1.GPIO13, R3.Pin_0
  N12: Mod1.GPIO19, R4.Pin_0
  N13: Mod1.GPIO26, R5.Pin_0
  N14: Mod1.GPIO21, R6.Pin_0
  N15: Language.Pin_3, Language.Pin_4, R7.Pin_0
  N16: modebtn.Pin_3, modebtn.Pin_4, R8.Pin_0
  VCC: J6.vcc, J7.vcc, J8.vcc, J9.vcc, J10.vcc, Part2.5.0V
  N17: J6.pulse, Part2.PWM2
  N18: J7.pulse, Part2.PWM3
  N19: J8.pulse, Part2.PWM1
  N20: J9.pulse, Part2.PWM4
  N21: J10.pulse, Part2.PWM0

notes:
  External Power Source
  (LithiumBattery)

custom parts:
  Adafruit PCA9685 PWM/Servo Breakout: Using only two pins, control 16 free-running PWM outputs! I2C-controlled PWM driver with a built in clock. Unlike the TLC5940 family, you do not need to continuously send it signal tying up your microcontroller, its completely free running! 5V compliant, which means you can control it from a 3.3V microcontroller and still safely drive up to 6V outputs (this is good for when you want to control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
