# Fritzing sketch pca-step-respeakers (saved by Fritzing 1.0.5)

parts:
  Mod1 = Raspberry Pi 4B  # not connected
  J6 = Basic Servo
  J7 = Basic Servo
  J8 = Basic Servo
  J9 = Basic Servo
  J10 = Basic Servo
  Part2 = Adafruit PCA9685 PWM/Servo Breakout [part_number=815]
  V2 = Pulse Power [initial_voltage=0V pulsed_voltage=5V period=100ms pulse_width=50ms duty_cycle=25% number_of_pulses=0 delay_time=0s internal_resistance=0.1Ω]  # not connected
  Pololu_A1 = Pololu A4988 [package=SO16]
  Part3 = Arduino Uno (Rev3) - ICSP
  CONN1 = USB connector [package=THT]  # not connected
  U1 = USB+SHIELD [package=usb-b-pth]  # not connected
  M1 = Stepper Motor - Unipolar
  U2 = LIPO-2000mAh [package=lipo-2000]  # not connected
  Part4 = Lilypad Power Supply
  Part5 = Lilypad Power Supply
  C1 = Electrolytic Capacitor [capacitance=100μF voltage=35V package="0807 [SMD, electrolytic]"]  # not connected
  SPKR1 = Loudspeaker  # not connected

nets:
  GND: J6.gnd, J7.gnd, J8.gnd, J9.gnd, J10.gnd, Part2.GND, Pololu_A1.GND#8, Part3.GND, Part4.GND
  VCC: J6.vcc, J7.vcc, J8.vcc, J9.vcc, J10.vcc, Part2.5.0V
  N1: J6.pulse, Part2.PWM2
  N2: J7.pulse, Part2.PWM3
  N3: J8.pulse, Part2.PWM1
  N4: J9.pulse, Part2.PWM4
  N5: J10.pulse, Part2.PWM0
  VCC_2: Part2.VCC, Pololu_A1.VDD, Part3.5V, Part4.+
  N6: Part2.SCL, Part3.A5/SCL
  N7: Part2.SDA, Part3.A4/SDA
  N8: Pololu_A1.1B, M1.B
  N9: Pololu_A1.1A, M1.C
  N10: Pololu_A1.2A, M1.COMMON_1
  N11: Pololu_A1.2B, M1.A
  N12: Pololu_A1.GND#14, Part5.GND
  N13: Pololu_A1.VMOT, Part5.+

notes:
  5v 3A
  Respeakers 2 mic
  12V
  5V
  Capacitor 100 μc

custom parts:
  Adafruit PCA9685 PWM/Servo Breakout: Using only two pins, control 16 free-running PWM outputs! I2C-controlled PWM driver with a built in clock. Unlike the TLC5940 family, you do not need to continuously send it signal tying up your microcontroller, its completely free running! 5V compliant, which means you can control it from a 3.3V microcontroller and still safely drive up to 6V outputs (this is good for when you want to control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
